// Digital circuit CPU.dig as structural Verilog
module CPU (
  input  CLK_RAW,
  input  [31:0] Breakpoint,
  output [31:0] x8_s0,
  output [31:0] x9_s1,
  output [31:0] x10_a0,
  output [31:0] PC,
  output [31:0] Address,
  output [31:0] Instr,
  output [7:0] Data_Read,
  output [5:0] Step,
  output [7:0] Substep,
  output [16:0] out_10,
  output [31:0] A,
  output [31:0] B,
  output [31:0] Result,
  output [11:0] CSR_Address,
  output [31:0] x11_a1,
  output [31:0] x4_tp,
  output [31:0] x5_t0,
  output [31:0] x6_t1,
  output [31:0] x7_t2,
  output [31:0] x1_ra,
  output [31:0] x2_sp,
  output [31:0] x3_gp,
  output [31:0] x12_a2,
  output [31:0] x13_a3,
  output [31:0] x14_a4,
  output [31:0] x15_a5,
  output [31:0] mepc,
  output [31:0] mscratch,
  output [31:0] mstatus,
  output [31:0] mie,
  output [31:0] mip,
  output [31:0] mcause,
  output [10:0] out_34,
  output [31:0] mtvec,
  output [7:0] Data_Write,
  output [31:0] Instr_2,
  output [31:0] Cycles,
  output [15:0] Instr16,
  output [4:0] Val,
  output out_42,
  output [4:0] Val_2,
  output out_44,
  output [7:0] Compr
);

  wire ADDR_CLK_GATED, ADDR_IN, ADDR_LATCH, ALU_A, ALU_AUX, ALU_B, ALU_N, and_1_out, and_5_out, B_INSTR,
       B_RESET, B_RUN, B_STEP, B_STOP, B_SUBSTEP, BUS_CLK, BUS_EN, BUT_INSTR, BUT_STOP, button_1_out,
       button_2_out, CLK, CNT_2, comparator_1_eq, comparator_1_gt, comparator_1_lt, comparator_2_eq, CS_IO,
       CS_RAM, CS_ROM, CSR_ADDR_LATCH, CSR_IN, CSR_IN_LATCH, CSR_OUT, CSR_OUT_LATCH, CSR_PC_OUT, d_ff_1_q,
       d_ff_2_q, d_ff_as_1_q, d_ff_as_2_nq, d_ff_as_3_q, d_ff_as_4_nq, d_ff_as_5_q, d_ff_as_6_q,
       diodeforward_1_out, Imm, INT1P, INT2P, INT3P, LASTSTEP, LED_G, LED_R, MEM_IN, MEM_OUT, MEPC_OUT,
       mie_1_mei1e, mie_1_mei2e, mie_1_mei3e, MIE_t, mip_1_mei1p, mip_1_mei2p, mip_1_mei3p, MRET, MTVEC_OUT,
       multiplexer_1_out, multiplexer_7_out, nADDR_CLK, nALU_RESET, nCLK, nILL_OP, nIRQ, nKB_INT, nLEN4,
       nMEM_OE, nMEM_OE_OUT, nMEM_WE, nMEM_WE_OUT, nOPDONE, not_2_out, not_3_out, not_4_out, not_5_out,
       nREG_IN_EN, nRESET, nS_EXT, nSTEPDONE, nWAIT, nWAKEUP, OP_IMM_LATCH, OP_IN, OP_IN_MUX, OP_LATCH,
       OP_LATCH_LSB, or_1_out, PC_CNT_EN, PC_IN, PC_IN_LATCH, PC_IN_MUX, PC_OUT, PC_OUT_LATCH, REG_IN, RESET,
       reset_2_out, RS1, SLEEP, switch_1_a, switchdt_1_p3, TRAP_OP;
  wire [0:0] LEN;
  wire [1:0] ALU_A_MUX, REG_IN_MUX, TRAP2;
  wire [2:0] ALU_OP, IMM_MUX;
  wire [3:0] RSA, RSB, RSD;
  wire [7:0] DATA, Mem_Dval;
  wire [20:19] MicroCode_d;
  wire [31:0] DATA_ADDR;

  // RGBLED rgbled_1: pin names not known; wires that end beside it: LED_R, LED_G, 1'b0
  Comparator #(.Bits(32)) comparator_1 (
    .a(x3_gp), .b(32'h1), .gt(comparator_1_gt), .eq(comparator_1_eq), .lt(comparator_1_lt));
  and and_1 (and_1_out, nIRQ, nILL_OP);
  // RGBLED rgbled_2: pin names not known; wires that end beside it: comparator_1_gt, comparator_1_eq, comparator_1_lt
  Comparator #(.Bits(32)) comparator_2 (.a(Breakpoint), .b(PC), .eq(comparator_2_eq));  // open: gt, lt
  Button #(.activeLow("true")) Stop (.out(BUT_STOP));
  Button #(.activeLow("true")) Run (.out(B_RUN));
  Button #(.activeLow("true")) u_Reset (.out(B_RESET));
  Switch switch_1 (.A(switch_1_a), .B(comparator_1_lt));
  D_FF d_ff_1 (.D(comparator_2_eq), .C(nOPDONE), .Q(d_ff_1_q));  // open: nQ
  Interrupt_Controller interrupt_controller_1 (
    .BUS_CLK(BUS_CLK), .OP_FETCH(OP_LATCH), .nTRAP(and_1_out), .nRESET(nRESET), .TRAP_OP(TRAP_OP),
    .TRAP_OP_FETCH(OP_IN_MUX));
  PullUp pullup_1 (.out(switch_1_a));
  D_FF_AS #(.Default(1)) d_ff_as_1 (.Set(nCLK), .D(1'b0), .C(d_ff_1_q), .Clr(1'b0), .Q(d_ff_as_1_q));  // open: nQ
  Button #(.activeLow("true")) One_Instruction (.out(BUT_INSTR));
  Button #(.activeLow("true")) One_Step (.out(B_STEP));
  Button #(.activeLow("true")) One_Substep (.out(B_SUBSTEP));
  D_FF #(.Default(1)) d_ff_2 (.D(switch_1_a), .C(~nOPDONE), .Q(d_ff_2_q));  // open: nQ
  DiodeBackward diodebackward_1 (.in(d_ff_2_q), .out(B_STOP));
  DiodeBackward diodebackward_2 (.in(BUT_STOP), .out(B_STOP));
  DiodeBackward diodebackward_3 (.in(d_ff_as_1_q), .out(B_INSTR));
  DiodeBackward diodebackward_4 (.in(BUT_INSTR), .out(B_INSTR));
  PullUp pullup_2 (.out(B_STOP));
  PullUp pullup_3 (.out(B_INSTR));
  Reset reset_2 (.out(reset_2_out));
  Multiplexer multiplexer_1 (.sel(ALU_A_MUX[0]), .in_0(RS1), .in_1(PC_OUT), .out(multiplexer_1_out));
  DebugShift32 debugshift32_1 (.CLK(BUS_CLK), .D(ALU_A), .nEN(1'b0), .Val(A));
  DebugShift32 debugshift32_2 (.CLK(BUS_CLK), .D(ALU_B), .nEN(1'b0), .Val(B));
  and and_2 (nRESET, reset_2_out, B_RESET);
  Multiplexer multiplexer_2 (.sel(ALU_A_MUX[1]), .in_0(multiplexer_1_out), .in_1(ALU_A_MUX[0]), .out(ALU_A));
  Mem mem_1 (
    .CLK(CLK), .BUS_CLK(BUS_CLK), .IN(MEM_IN), .ADDR_IN(ADDR_IN), .ADDR_LATCH(ADDR_LATCH),
    .ADDR_CLK(ADDR_CLK_GATED), .nOE(nMEM_OE), .nWE(nMEM_WE), .nS_EXT(nS_EXT), .nRESET(nRESET), .OUT(MEM_OUT),
    .DATA(DATA), .DATA_ADDR(DATA_ADDR), .DAddr(Address), .DVal(Mem_Dval), .nMEM_OE_OUT(nMEM_OE_OUT),
    .nMEM_WE_OUT(nMEM_WE_OUT));  // open: DIn
  D_FF #(.Bits(8)) d_ff_3 (.D(DATA), .C(nMEM_OE_OUT), .Q(Data_Read));  // open: nQ
  D_FF #(.Bits(8)) d_ff_4 (.D(DATA), .C(nMEM_WE_OUT), .Q(Data_Write));  // open: nQ
  not not_1 (RESET, nRESET);
  Clock_driver clock_driver_1 (
    .CLK_RAW(CLK_RAW), .Stop(B_STOP), .Run(B_RUN), .One_Instruction(B_INSTR), .One_Step(B_STEP),
    .One_Substep(B_SUBSTEP), .nSTEPDONE(nSTEPDONE), .nOPDONE(nOPDONE), .nRESET(nRESET), .nWAKEUP(nWAKEUP),
    .SLEEP(SLEEP), .nWAIT(nWAIT), .CLK(CLK), .nCLK(nCLK), .LED_R(LED_R), .LED_G(LED_G));
  nand nand_1 (nLEN4, LEN[0], BUS_EN);
  or or_1 (or_1_out, IMM_MUX[0], IMM_MUX[1], IMM_MUX[2]);
  DebugShift32 debugshift32_3 (.CLK(BUS_CLK), .D(ADDR_IN), .nEN(1'b0), .Val(Result));
  nor nor_1 (ADDR_CLK_GATED, nADDR_CLK, CNT_2);
  Multiplexer multiplexer_3 (.sel(or_1_out), .in_0(MEM_IN), .in_1(Imm), .out(ALU_B));
  PullUp pullup_4 (.out(nWAIT));
  nor nor_2 (LASTSTEP, LEN[0], BUS_EN);
  not not_2 (not_2_out, BUS_CLK);
  not not_3 (not_3_out, nRESET);
  D_FF_AS d_ff_as_2 (.Set(~1'b1), .D(d_ff_as_2_nq), .C(BUS_CLK), .Clr(~nRESET), .Q(Val[0]), .nQ(d_ff_as_2_nq));
  Clock clock_1 (
    .CLK(CLK), .nCLK(nCLK), .nLEN4(nLEN4), .LASTSTEP(LASTSTEP), .nRESET(nRESET), .STEP(out_10[5:0]),
    .STEPDONE(nSTEPDONE), .SUBSTEP(Substep), .OPDONE(nOPDONE));
  ALU alu_1 (
    .BUS_CLK(BUS_CLK), .A(ALU_A), .B(ALU_B), .N(ALU_N), .ALU_nRESET(nALU_RESET), .ALU_AUX(ALU_AUX),
    .S(ALU_OP), .FLAG(out_10[16]), .OUT(ADDR_IN));  // open: DLEN, DSUM, C
  // SwitchDT switchdt_1: pin names not known; wires that end beside it: nMEM_WE_OUT, 1'b1, switchdt_1_p3
  Terminal terminal_1 (
    .A(DATA_ADDR[15:0]), .nCS(CS_IO), .nWE(nMEM_WE_OUT), .nOE(nMEM_OE_OUT), .D(DATA), .nINT(nKB_INT));
  _74HC4024 _74hc4024_1 (
    .CP(not_2_out), .MR(not_3_out), .Q0(Val_2[0]), .Q1(Val_2[1]), .Q2(Val_2[2]), .Q3(Val_2[3]), .Q4(Val_2[4]));  // open: Q5, Q6
  EEPROM #(.AddrBits(16), .Bits(8)) Firmware (
    .A(DATA_ADDR[15:0]), .CS(~CS_ROM), .WE(~switchdt_1_p3), .OE(~nMEM_OE_OUT), .D(DATA));
  RAMSinglePortSel #(.AddrBits(16), .Bits(8)) RAM (
    .A(DATA_ADDR[15:0]), .CS(~CS_RAM), .WE(~nMEM_WE_OUT), .OE(~nMEM_OE_OUT), .D(DATA));
  Demultiplexer #(.Selector_Bits(2), .Default(1)) demultiplexer_1 (
    .sel(DATA_ADDR[31:30]), .in(1'b0), .out_0(CS_ROM), .out_2(CS_RAM), .out_3(CS_IO));  // open: out_1
  or or_2 (out_44, BUS_EN, Val_2[3], Val_2[4]);
  and and_3 (BUS_CLK, CLK, BUS_EN);
  // _74161 _74161_1: pin names not known; wires that end beside it: 1'b1, nRESET, d_ff_as_2_nq, 1'b1, 1'b1, 1'b0, 1'b0, 1'b0, 1'b0, 1'b1, 1'b0, Val[1], Val[2], Val[3], Val[4]
  Multiplexer multiplexer_4 (.sel(PC_IN_MUX), .in_0(ADDR_IN), .in_1(CSR_PC_OUT), .out(PC_IN));
  Multiplexer multiplexer_5 (.sel(OP_IN_MUX), .in_0(MEM_OUT), .in_1(TRAP_OP), .out(OP_IN));
  D_FF d_ff_5 (.D(PC_CNT_EN), .C(CLK), .Q(OP_IMM_LATCH));  // open: nQ
  D_FF_AS d_ff_as_3 (.Set(~nRESET), .D(OP_LATCH), .C(CLK), .Clr(1'b0), .Q(d_ff_as_3_q));  // open: nQ
  ROM #(.AddrBits(17), .isProgramMemory("true"), .Bits(32)) MicroCode (
    .A(out_10), .sel(1'b1),
    .D({REG_IN_MUX, IMM_MUX, ALU_A_MUX, PC_IN_MUX, CSR_IN_LATCH, CSR_OUT_LATCH, CSR_ADDR_LATCH, MicroCode_d, OP_LATCH_LSB, nALU_RESET, ALU_AUX, ALU_OP, ALU_N, nREG_IN_EN, nMEM_WE, nMEM_OE, nADDR_CLK, ADDR_LATCH, nILL_OP, PC_OUT_LATCH, PC_IN_LATCH, OP_LATCH, SLEEP, BUS_EN, LEN[0]}));
  PC pc_1 (
    .CLK(CLK), .BUS_CLK(BUS_CLK), .IN(PC_IN), .IN_LATCH(PC_IN_LATCH), .OUT_LATCH(PC_OUT_LATCH),
    .OUT_SnP(out_44), .CNT_EN(PC_CNT_EN), .CNT_2(CNT_2), .nRESET(nRESET), .OUT(PC_OUT), .PC(PC));
  D_FF_AS d_ff_as_4 (.Set(~nRESET), .D(d_ff_as_3_q), .C(nCLK), .Clr(1'b0), .nQ(d_ff_as_4_nq));  // open: Q
  OpCode opcode_1 (
    .BUS_CLK(BUS_CLK), .IN(OP_IN), .OP_LATCH(OP_LATCH), .OP_LATCH_LSB(OP_LATCH_LSB),
    .IMM_LATCH(OP_IMM_LATCH), .IMM_SnP(out_44), .IMM_MUX(IMM_MUX), .nRESET(nRESET), .IMM(Imm), .RSA(RSA),
    .RSB(RSB), .RD(RSD), .OPCODE(out_10[10:6]), .FUNC3(out_10[13:11]), .ALU_SA(out_10[15]), .nS_EXT(nS_EXT),
    .SYS(out_10[14]), .TRAP2(TRAP2), .CNT_2(CNT_2), .Instr(Instr), .Instr16(Instr16), .Instr8(Compr));
  or or_3 (out_42, BUS_EN, Val[3], Val[4]);
  and and_4 (PC_CNT_EN, OP_LATCH, d_ff_as_4_nq);
  Register_bank register_bank_1 (
    .CLK(BUS_CLK), .IN(REG_IN), .nEN_IN(nREG_IN_EN), .SA(RSA), .SB(RSB), .SD(RSD), .RESET(RESET), .A(RS1),
    .B(MEM_IN));
  Register_view register_view_1 (
    .BUS_CLK(BUS_CLK), .nREG_IN_EN(nREG_IN_EN), .REG_IN(REG_IN), .RSD(RSD), .x1_ra(x1_ra), .x2_sp(x2_sp),
    .x3_gp(x3_gp), .x4_tp(x4_tp), .x5_t0(x5_t0), .x6_t1(x6_t1), .x7_t2(x7_t2), .x8_s0_fp(x8_s0),
    .x9_s1(x9_s1), .x10_a0(x10_a0), .x11_a1(x11_a1), .x12_a2(x12_a2), .x13_a3(x13_a3), .x14_a4(x14_a4),
    .x15_a5(x15_a5));
  Multiplexer #(.Selector_Bits(2)) multiplexer_6 (
    .sel(REG_IN_MUX), .in_0(ADDR_IN), .in_1(MEM_OUT), .in_2(CSR_IN), .in_3(PC_OUT), .out(REG_IN));
  Button #(.activeLow("true")) button_1 (.out(button_1_out));
  Button #(.activeLow("true")) button_2 (.out(button_2_out));
  not not_4 (not_4_out, MRET);
  Multiplexer multiplexer_7 (.sel(out_10[13]), .in_0(RS1), .in_1(Imm), .out(multiplexer_7_out));
  PullDown pulldown_1 (.out(CSR_IN));
  and and_5 (and_5_out, not_4_out, PC_IN_MUX);
  D_FF_AS #(.Default(1)) d_ff_as_5 (.Set(CLK), .D(1'b0), .C(PC_IN_MUX), .Clr(1'b0), .Q(d_ff_as_5_q));  // open: nQ
  Counter #(.Bits(32)) counter_1 (.en(1'b1), .C(CLK), .clr(1'b0), .out(Cycles));  // open: ovf
  MIE mie_1 (
    .CLK(CLK), .BUS_CLK(BUS_CLK), .CSR_IN(CSR_OUT), .CSR_IN_LATCH(CSR_IN_LATCH),
    .CSR_OUT_LATCH(CSR_OUT_LATCH), .CSR_ADDR(CSR_Address), .nRESET(nRESET), .CSR_OUT(CSR_IN), .mie(mie),
    .MEI1E(mie_1_mei1e), .MEI2E(mie_1_mei2e), .MEI3E(mie_1_mei3e));
  MIP mip_1 (
    .CLK(CLK), .BUS_CLK(BUS_CLK), .CSR_IN(CSR_OUT), .CSR_IN_LATCH(CSR_IN_LATCH),
    .CSR_OUT_LATCH(CSR_OUT_LATCH), .CSR_ADDR(CSR_Address), .nINT1(nKB_INT), .nINT2(button_1_out),
    .nINT3(button_2_out), .nRESET(nRESET), .CSR_OUT(CSR_IN), .mip(mip), .MEI1P(mip_1_mei1p),
    .MEI2P(mip_1_mei2p), .MEI3P(mip_1_mei3p));
  MEPC mepc_1 (
    .BUS_CLK(BUS_CLK), .PC_IN(PC_OUT), .IN_EN(and_5_out), .CSR_IN(CSR_OUT), .CSR_IN_LATCH(CSR_IN_LATCH),
    .CSR_ADDR(CSR_Address), .RESET(RESET), .OUT(MEPC_OUT), .CSR_OUT(CSR_IN), .mepc(mepc));
  MSTATUS mstatus_1 (
    .CLK(CLK), .BUS_CLK(BUS_CLK), .CSR_IN(CSR_OUT), .CSR_IN_LATCH(CSR_IN_LATCH),
    .CSR_OUT_LATCH(CSR_OUT_LATCH), .CSR_ADDR(CSR_Address), .IRQ(PC_IN_MUX), .MRET(MRET),
    .IRQ_LATCH(d_ff_as_5_q), .RESET(RESET), .nRESET(nRESET), .CSR_OUT(CSR_IN), .mstatus(mstatus), .MIE(MIE_t));  // open: MPIE
  CSR csr_1 (
    .CLK(BUS_CLK), .INA(multiplexer_7_out), .INB(CSR_IN), .CSR_FUNC(out_10[12:11]), .ADDR_IN(Imm),
    .ADDR_LATCH(CSR_ADDR_LATCH), .nRESET(nRESET), .NEW_VAL(CSR_OUT), .ADDR(CSR_Address));
  Counter #(.Bits(32)) counter_2 (.en(1'b1), .C(~nOPDONE), .clr(1'b0), .out(Instr_2));  // open: ovf
  D_FF_AS #(.Default(1)) d_ff_as_6 (.Set(CLK), .D(MRET), .C(PC_IN_MUX), .Clr(1'b0), .Q(d_ff_as_6_q));  // open: nQ
  and and_6 (INT1P, mie_1_mei1e, mip_1_mei1p);
  and and_7 (INT2P, mie_1_mei2e, mip_1_mei2p);
  and and_8 (INT3P, mie_1_mei3e, mip_1_mei3p);
  not not_5 (not_5_out, TRAP2[0]);
  and and_9 (MRET, not_5_out, TRAP2[1]);
  MTVEC mtvec_1 (
    .BUS_CLK(BUS_CLK), .MTVEC_SnP(PC_IN_MUX), .CSR_IN(CSR_OUT), .CSR_IN_LATCH(CSR_IN_LATCH),
    .CSR_ADDR(CSR_Address), .RESET(RESET), .MTVEC_OUT(MTVEC_OUT), .CSR_OUT(CSR_IN), .mtvec(mtvec));
  MSCRATCH mscratch_1 (
    .BUS_CLK(BUS_CLK), .CSR_IN(CSR_OUT), .CSR_IN_LATCH(CSR_IN_LATCH), .CSR_ADDR(CSR_Address), .RESET(RESET),
    .CSR_OUT(CSR_IN), .mscratch(mscratch));
  MCAUSE mcause_1 (
    .BUS_CLK(BUS_CLK), .CSR_IN_LATCH(CSR_IN_LATCH), .CSR_OUT_LATCH(CSR_OUT_LATCH), .CSR_ADDR(CSR_Address),
    .TRAP2(TRAP2), .nIRQ(nIRQ), .INT1P(INT1P), .INT2P(INT2P), .INT3P(INT3P), .IRQ_LATCH(d_ff_as_6_q),
    .nRESET(nRESET), .CSR_OUT(CSR_IN), .mcause(mcause));
  DiodeForward diodeforward_1 (.in(INT1P), .out(diodeforward_1_out));
  DiodeForward diodeforward_2 (.in(INT2P), .out(diodeforward_1_out));
  DiodeForward diodeforward_3 (.in(INT3P), .out(diodeforward_1_out));
  Multiplexer multiplexer_8 (.sel(MRET), .in_0(MTVEC_OUT), .in_1(MEPC_OUT), .out(CSR_PC_OUT));
  PullDown pulldown_2 (.out(diodeforward_1_out));
  not not_6 (nWAKEUP, diodeforward_1_out);
  nand nand_2 (nIRQ, MIE_t, diodeforward_1_out);
  // Pins of 1 and 8 bits meet at Compr

  assign out_34 = out_10[16:6];
  assign Step = out_10[5:0];

  // Other names for the same wires on the sheet: LEN[1] = BUS_EN; ALU_OUT = ADDR_IN; CntCycles[31:0] = Cycles;
  //   CntInstr[31:0] = Instr_2; CSR_ADDR[11:0] = CSR_Address; Da[31:0] = A; DATA_ADDR_16[15:0] = DATA_ADDR[15:0];
  //   Db[31:0] = B; Dres[31:0] = Result; FLAG = out_10[16]; FUNC3[2:0] = out_10[13:11]; Mem_Addr[31:0] = Address;
  //   Mem_Data_R[7:0] = Data_Read; Mem_Data_W[7:0] = Data_Write; OPCODE[4:0] = out_10[10:6]; IMM_PC_OUT_SnP = out_44;
  //   IMM_SnP = out_44; PC_OUT_SnP = out_44; RS2 = MEM_IN; SA = out_10[15]; SYS = out_10[14]; x1[31:0] = x1_ra;
  //   x2[31:0] = x2_sp; x3[31:0] = x3_gp; x4[31:0] = x4_tp; x5[31:0] = x5_t0; x6[31:0] = x6_t1; x7[31:0] = x7_t2;
  //   x8[31:0] = x8_s0; x9[31:0] = x9_s1; x10[31:0] = x10_a0; x11[31:0] = x11_a1; x12[31:0] = x12_a2;
  //   x13[31:0] = x13_a3; x14[31:0] = x14_a4; x15[31:0] = x15_a5

  // Notes on the sheet:
  //   CLK_RAW: Hz: 4000000
  //   Breakpoint: default 4294967295
  //   Debug
  //   Interrupts
  //   Clock
  //   ALU
  //   Memory
  //   Invert LASTSTEP.
  //   Also in clock
  //   and in interrupt controller
  //   contents of Firmware (hex, n*v repeats v):
  //   81,40,1,41,33,87,20,0,81,43,b7,4,2,0,89,4,5,4,63,4,77,0,6f,70
  //   ,20,6f,85,40,5,41,33,87,20,0,89,43,b7,4,2,0,8d,4,5,4,63,4,77,0
  //   ,6f,70,80,6d,8d,40,1d,41,33,87,20,0,a9,43,b7,4,2,0,91,4,5,4,63
  //   ,4,77,0,6f,70,e0,6b,81,40,37,81,ff,ff,33,87,20,0,e1,73,b7,4,2
  //   ,0,95,4,5,4,63,4,77,0,6f,70,20,6a,b7,0,0,80,1,41,33,87,20,0,b7
  //   ,3,0,80,b7,4,2,0,99,4,5,4,63,4,77,0,6f,70,40,68,b7,0,0,80,37,81
  //   ,ff,ff,33,87,20,0,b7,83,ff,7f,b7,4,2,0,9d,4,5,4,63,4,77,0,6f,70
  //   ,40,66,81,40,37,81,0,0,7d,11,33,87,20,0,a1,63,fd,13,b7,4,2,0,a1
  //   ,4,5,4,63,4,77,0,6f,70,40,64,b7,0,0,80,fd,10,1,41,33,87,20,0,b7
  //   ,3,0,80,fd,13,b7,4,2,0,a5,4,5,4,63,4,77,0,6f,70,20,62,b7,0,0,80
  //   ,fd,10,37,81,0,0,7d,11,33,87,20,0,b7,83,0,80,f9,13,b7,4,2,0,a9
  //   ,4,5,4,63,4,77,0,6f,70,c0,5f,b7,0,0,80,37,81,0,0,7d,11,33,87,20
  //   ,0,b7,83,0,80,fd,13,b7,4,2,0,ad,4,5,4,63,4,77,0,6f,70,80,5d,b7
  //   ,0,0,80,fd,10,37,81,ff,ff,33,87,20,0,b7,83,ff,7f,fd,13,b7,4,2
  //   ,0,b1,4,5,4,63,4,77,0,6f,70,40,5b,81,40,13,1,f0,ff,33,87,20,0
  //   ,93,3,f0,ff,b7,4,2,0,b5,4,5,4,63,4,77,0,6f,70,60,59,93,0,f0,ff
  //   ,5,41,33,87,20,0,81,43,b7,4,2,0,b9,4,5,4,63,4,77,0,6f,70,a0,57
  //   ,93,0,f0,ff,13,1,f0,ff,33,87,20,0,93,3,e0,ff,b7,4,2,0,bd,4,5,4
  //   ,63,4,77,0,6f,70,a0,55,85,40,37,1,0,80,7d,11,33,87,20,0,b7,3,0
  //   ,80,b7,4,2,0,c1,4,5,4,63,4,77,0,6f,70,a0,53,b5,40,2d,41,8a,90
  //   ,e1,43,b7,4,2,0,c5,4,5,4,63,84,70,0,6f,70,20,52,b9,40,2d,41,6
  //   ,91,e5,43,b7,4,2,0,c9,4,5,4,63,4,71,0,6f,70,a0,50,b5,40,86,90
  //   ,e9,43,b7,4,2,0,cd,4,5,4,63,84,70,0,6f,70,40,4f,1,42,b5,40,2d
  //   ,41,33,87,20,0,3a,83,5,2,89,42,e3,19,52,fe,e1,43,b7,4,2,0,d1,4
  //   ,5,4,63,4,73,0,6f,70,e0,4c,1,42,b9,40,2d,41,33,87,20,0,1,0,3a
  //   ,83,5,2,89,42,e3,18,52,fe,e5,43,b7,4,2,0,d5,4,5,4,63,4,73,0,6f
  //   ,70,60,4a,1,42,bd,40,2d,41,33,87,20,0,1,0,1,0,3a,83,5,2,89,42
  //   ,e3,17,52,fe,e9,43,b7,4,2,0,d9,4,5,4,63,4,73,0,6f,70,c0,47,1,42
  //   ,b5,40,2d,41,33,87,20,0,5,2,89,42,e3,1a,52,fe,e1,43,b7,4,2,0,dd
  //   ,4,5,4,63,4,77,0,6f,70,80,45,1,42,b9,40,2d,41,1,0,33,87,20,0,5
  //   ,2,89,42,e3,19,52,fe,e5,43,b7,4,2,0,e1,4,5,4,63,4,77,0,6f,70,20
  //   ,43,1,42,bd,40,2d,41,1,0,1,0,33,87,20,0,5,2,89,42,e3,18,52,fe
  //   ,e9,43,b7,4,2,0,e5,4,5,4,63,4,77,0,6f,70,a0,40,1,42,b5,40,1,0
  //   ,2d,41,33,87,20,0,5,2,89,42,e3,19,52,fe,e1,43,b7,4,2,0,e9,4,5
  //   ,4,63,4,77,0,6f,70,40,3e,1,42,b9,40,1,0,2d,41,1,0,33,87,20,0,5
  //   ,2,89,42,e3,18,52,fe,e5,43,b7,4,2,0,ed,4,5,4,63,4,77,0,6f,70,c0
  //   ,3b,1,42,bd,40,1,0,1,0,2d,41,33,87,20,0,5,2,89,42,e3,18,52,fe
  //   ,e9,43,b7,4,2,0,f1,4,5,4,63,4,77,0,6f,70,40,39,1,42,2d,41,b5,40
  //   ,33,87,20,0,5,2,89,42,e3,1a,52,fe,e1,43,b7,4,2,0,f5,4,5,4,63,4
  //   ,77,0,6f,70,0,37,1,42,2d,41,b9,40,1,0,33,87,20,0,5,2,89,42,e3
  //   ,19,52,fe,e5,43,b7,4,2,0,f9,4,5,4,63,4,77,0,6f,70,a0,34,1,42,2d
  //   ,41,bd,40,1,0,1,0,33,87,20,0,5,2,89,42,e3,18,52,fe,e9,43,b7,4
  //   ,2,0,fd,4,5,4,63,4,77,0,6f,70,20,32,1,42,2d,41,1,0,b5,40,33,87
  //   ,20,0,5,2,89,42,e3,19,52,fe,e1,43,b7,4,2,0,93,84,4,2,5,4,63,4
  //   ,77,0,6f,70,a0,2f,1,42,2d,41,1,0,b9,40,1,0,33,87,20,0,5,2,89,42
  //   ,e3,18,52,fe,e5,43,b7,4,2,0,93,84,14,2,5,4,63,4,77,0,6f,70,0,2d
  //   ,1,42,2d,41,1,0,1,0,bd,40,33,87,20,0,5,2,89,42,e3,18,52,fe,e9
  //   ,43,b7,4,2,0,93,84,24,2,5,4,63,4,77,0,6f,70,60,2a,bd,40,6,81,bd
  //   ,43,b7,4,2,0,93,84,34,2,5,4,63,4,71,0,6f,70,e0,28,93,0,0,2,33
  //   ,81,0,0,93,3,0,2,b7,4,2,0,93,84,44,2,5,4,63,4,71,0,6f,70,0,27
  //   ,b3,0,0,0,81,43,b7,4,2,0,93,84,54,2,5,4,63,84,70,0,6f,70,80,25
  //   ,c1,40,79,41,33,80,20,0,81,43,b7,4,2,0,93,84,64,2,5,4,63,4,70
  //   ,0,6f,70,c0,23,81,40,1,41,33,87,20,40,81,43,b7,4,3,0,89,4,5,4
  //   ,63,4,77,0,6f,70,20,22,85,40,5,41,33,87,20,40,81,43,b7,4,3,0,8d
  //   ,4,5,4,63,4,77,0,6f,70,80,20,8d,40,1d,41,33,87,20,40,93,3,c0,ff
  //   ,b7,4,3,0,91,4,5,4,63,4,77,0,6f,70,c0,1e,81,40,37,81,ff,ff,33
  //   ,87,20,40,a1,63,b7,4,3,0,95,4,5,4,63,4,77,0,6f,70,0,1d,b7,0,0
  //   ,80,1,41,33,87,20,40,b7,3,0,80,b7,4,3,0,99,4,5,4,63,4,77,0,6f
  //   ,70,20,1b,b7,0,0,80,37,81,ff,ff,33,87,20,40,b7,83,0,80,b7,4,3
  //   ,0,9d,4,5,4,63,4,77,0,6f,70,20,19,81,40,37,81,0,0,7d,11,33,87
  //   ,20,40,e1,73,85,3,b7,4,3,0,a1,4,5,4,63,4,77,0,6f,70,20,17,b7,0,0
  //   ,80,fd,10,1,41,33,87,20,40,b7,3,0,80,fd,13,b7,4,3,0,a5,4,5,4,63
  //   ,4,77,0,6f,70,0,15,b7,0,0,80,fd,10,37,81,0,0,7d,11,33,87,20,40
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  //   PC
  //   Opcode
  //   Microcode
  //   contents of MicroCode (hex, n*v repeats v):
  //   a10e49,8*8ab0e4b,a30ee9,a30f49,a30c49,8*72ab264b,a306c9,a30749
  //   ,a30c61,a30e43,a30f43,a30c41,a30e43,a30f43,a70c41,a70e43,a70f43
  //   ,a70c41,a70e43,a70f43,a30e40,29*0,a30e49,a30e09,8*32ab2e0b,a30e89
  //   ,a30f01,a30c01,a30e03,a30f03,a30c01,a30e03,a30f03,a70c01,a70e03
  //   ,a70f03,a70c01,a70e03,a70f03,a30e00,39*0,a30e49,a30e09,8*32ab2e0b
  //   ,a30e89,a30f01,a30c01,a30e03,a30f03,a30c01,a30e03,a30f03,a70c01
  //   ,a70e03,a70f03,a70c01,a70e03,a70f03,a30e00,39*0,a30e49,a30c61
  //   ,a30e43,a30f43,a30c41,a30e43,a30f43,a70c41,a70e43,a70f43,a70c41
  //   ,a70e43,a70f43,a30e40,50*0,a10c49,8ab0643,8ab0743,8ab0461,8ab0643
  //   ,8ab0743,8af0441,8af0643,8af0743,8af0441,8af0643,8af0743,a30e40
  //   ,51*0,a10c49,22ab0643,22ab0743,22ab0461,22ab0643,22ab0743,22af0441
  //   ,22af0643,22af0743,22af0441,22af0643,22af0743,a30e40,51*0,a30e49
  //   ,a30e09,8*32ab2e0b,a30e89,a30f01,a30c01,a30e03,a30f03,a30c01,a30e03
  //   ,a30f03,a70c01,a70e03,a70f03,a70c01,a70e03,a70f03,a30e00,39*0
  //   ,a30e49,a30e09,8*32ab2e0b,a30e89,a30f01,a30c01,a30e03,a30f03,a30c01
  //   ,a30e03,a30f03,a70c01,a70e03,a70f03,a70c01,a70e03,a70f03,a30e00
  //   ,39*0,a10e49,8*10ab0e4b,a30ee9,32ab2ecb,32ab2f4b,32ab2a49,6*32ab2e4b
  //   ,a30ec9,a30f49,a30c61,a30e43,a30f43,a30c41,a30e43,a30f43,a70c41
  //   ,a70e43,a70f43,a70c41,a70e43,a70f43,a30e40,30*0,a30e49,a30e09
  //   ,8*32ab2e0b,a30e89,a30f01,a30c01,a30e03,a30f03,a30c01,a30e03,a30f03
  //   ,a70c01,a70e03,a70f03,a70c01,a70e03,a70f03,a30e00,39*0,a30e49
  //   ,a30e09,8*32ab2e0b,a30e89,a30f01,a30c01,a30e03,a30f03,a30c01,a30e03
  //   ,a30f03,a70c01,a70e03,a70f03,a70c01,a70e03,a70f03,a30e00,39*0
  //   ,a30e49,a30e09,8*32ab2e0b,a30e89,a30f01,a30c01,a30e03,a30f03,a30c01
  //   ,a30e03,a30f03,a70c01,a70e03,a70f03,a70c01,a70e03,a70f03,a30e00
  //   ,39*0,a10c49,ab0643,ab0743,ab0461,ab0643,ab0743,af0441,af0643
  //   ,af0743,af0441,af0643,af0743,a30e40,51*0,a10c49,24ab0643,24ab0743
  //   ,24ab0461,24ab0643,24ab0743,24af0441,24af0643,24af0743,24af0441
  //   ,24af0643,24af0743,a30e40,51*0,a30e49,a30e09,8*32ab2e0b,a30e89
  //   ,a30f01,a30c01,a30e03,a30f03,a30c01,a30e03,a30f03,a70c01,a70e03
  //   ,a70f03,a70c01,a70e03,a70f03,a30e00,39*0,a30e49,a30e09,8*32ab2e0b
  //   ,a30e89,a30f01,a30c01,a30e03,a30f03,a30c01,a30e03,a30f03,a70c01
  //   ,a70e03,a70f03,a70c01,a70e03,a70f03,a30e00,39*0,a30e49,a30e09
  //   ,8*32ab2e0b,a30e89,a30f01,a30c01,a30e03,a30f03,a30c01,a30e03,a30f03
  //   ,a70c01,a70e03,a70f03,a70c01,a70e03,a70f03,a30e00,39*0,a30e49
  //   ,a30e09,8*32ab2e0b,a30e89,a30f01,a30c01,a30e03,a30f03,a30c01,a30e03
  //   ,a30f03,a70c01,a70e03,a70f03,a70c01,a70e03,a70f03,a30e00,39*0
  //   ,a30e49,a30e09,8*32ab2e0b,a30e89,a30f01,a30c01,a30e03,a30f03,a30c01
  //   ,a30e03,a30f03,a70c01,a70e03,a70f03,a70c01,a70e03,a70f03,a30e00
  //   ,39*0,a30e49,a30e09,8*32ab2e0b,a30e89,a30f01,a30c01,a30e03,a30f03
  //   ,a30c01,a30e03,a30f03,a70c01,a70e03,a70f03,a70c01,a70e03,a70f03
  //   ,a30e00,39*0,a30e49,a30e09,8*32ab2e0b,a30e89,a30f01,a30c01,a30e03
  //   ,a30f03,a30c01,a30e03,a30f03,a70c01,a70e03,a70f03,a70c01,a70e03
  //   ,a70f03,a30e00,39*0,a30e49,a30e09,8*32ab2e0b,a30e89,a30f01,a30c01
  //   ,a30e03,a30f03,a30c01,a30e03,a30f03,a70c01,a70e03,a70f03,a70c01
  //   ,a70e03,a70f03,a30e00,39*0,a30e49,a30e09,8*32ab2e0b,a30e89,a30f01
  //   ,a30c01,a30e03,a30f03,a30c01,a30e03,a30f03,a70c01,a70e03,a70f03
  //   ,a70c01,a70e03,a70f03,a30e00,39*0,a30e49,a30e09,8*32ab2e0b,a30e89
  //   ,a30f01,a30c01,a30e03,a30f03,a30c01,a30e03,a30f03,a70c01,a70e03
  //   ,a70f03,a70c01,a70e03,a70f03,a30e00,39*0,a11e49,8*aa5e4b,a30e49
  //   ,a30c61,a30e43,a30f43,a30c41,a30e43,a30f43,a70c41,a70e43,a70f43
  //   ,a70c41,a70e43,a70f43,a30e40,41*0,a10e49,8*8ab0e4b,a10ee9,a10f59
  //   ,a10c49,32ab2643,32ab2743,32ab2441,32ab2643,32ab2743,32af2441
  //   ,32af2643,32af2743,32af2441,32af2643,32af2743,a30e60,40*0,a30e49
  //   ,a30e09,8*32ab2e0b,a30e89,a30f01,a30c01,a30e03,a30f03,a30c01,a30e03
  //   ,a30f03,a70c01,a70e03,a70f03,a70c01,a70e03,a70f03,a30e00,39*0
  //   ,a10e49,8*2aab0e4b,a10ee9,a10f59,a10c49,32ab2643,32ab2743,32ab2441
  //   ,32ab2643,32ab2743,32af2441,32af2643,32af2743,32af2441,32af2643
  //   ,32af2743,a30e60,40*0,a30e49,8*1ab0e4b,ab0e59,ab0e69,8*32ab2e4b
  //   ,a30ec9,a30f41,a30c41,a30e43,a30f43,a30c41,a30e43,a30f43,a70c41
  //   ,a70e43,a70f43,a70c41,a70e43,a70f43,a30e40,30*0,a30e49,a30e09
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  //   Registers
  //   CSR
endmodule
