// Digital circuit Clock-driver.dig as structural Verilog
module Clock_driver (
  input  CLK_RAW,
  input  Stop,
  input  Run,
  input  One_Instruction,
  input  One_Step,
  input  One_Substep,
  input  nSTEPDONE,
  input  OP_LATCH,
  input  nRESET,
  input  nWAKEUP,
  input  SLEEP,
  input  nWAIT_DONE,
  input  nWAIT,
  output CLK,
  output nCLK,
  output Running
);

  wire and_1_out, and_2_out, CLK_EN, d_ff_as_1_q, d_ff_as_2_q, d_ff_as_3_nq, d_ff_as_4_nq,
       diodebackward_1_out, diodebackward_2_out, diodebackward_3_out, diodeforward_1_out, nor_1_out,
       not_2_out, nRAWCLK, pullup_1_out, pullup_5_out, rs_ff_as_1_q, rs_ff_as_2_nq, rs_ff_as_3_q;

  not not_1 (nRAWCLK, CLK_RAW);
  DiodeBackward diodebackward_1 (.in(nRESET), .out(diodebackward_1_out));
  DiodeBackward diodebackward_2 (.in(nRESET), .out(diodebackward_2_out));
  DiodeBackward diodebackward_3 (.in(nRESET), .out(diodebackward_3_out));
  PullUp pullup_1 (.out(pullup_1_out));
  PullUp pullup_2 (.out(diodebackward_1_out));
  PullUp pullup_3 (.out(diodebackward_2_out));
  PullUp pullup_4 (.out(diodebackward_3_out));
  DiodeBackward diodebackward_4 (.in(Stop), .out(diodebackward_1_out));
  DiodeBackward diodebackward_5 (.in(Stop), .out(diodebackward_2_out));
  DiodeBackward diodebackward_6 (.in(Stop), .out(diodebackward_3_out));
  DiodeBackward diodebackward_7 (.in(One_Instruction), .out(pullup_1_out));
  DiodeBackward diodebackward_8 (.in(One_Instruction), .out(diodebackward_3_out));
  JK_FF jk_ff_1 (.J(CLK_EN), .C(CLK_RAW), .K(CLK_EN), .Q(CLK), .nQ(nCLK));
  DiodeBackward diodebackward_9 (.in(One_Step), .out(pullup_1_out));
  DiodeBackward diodebackward_10 (.in(One_Step), .out(diodebackward_2_out));
  DiodeBackward diodebackward_11 (.in(One_Step), .out(diodebackward_3_out));
  DiodeBackward diodebackward_12 (.in(One_Substep), .out(pullup_1_out));
  DiodeBackward diodebackward_13 (.in(One_Substep), .out(diodebackward_1_out));
  DiodeBackward diodebackward_14 (.in(One_Substep), .out(diodebackward_2_out));
  DiodeBackward diodebackward_15 (.in(One_Substep), .out(diodebackward_3_out));
  D_FF_AS d_ff_as_1 (.Set(~nRESET), .D(1'b1), .C(nRAWCLK), .Clr(~pullup_1_out), .Q(d_ff_as_1_q));  // open: nQ
  RS_FF_AS rs_ff_as_1 (.S(~One_Step), .R(~diodebackward_1_out), .Q(rs_ff_as_1_q));  // open: nQ
  RS_FF_AS rs_ff_as_2 (.S(~One_Instruction), .R(~diodebackward_2_out), .nQ(rs_ff_as_2_nq));  // open: Q
  RS_FF_AS rs_ff_as_3 (.S(~Run), .R(~diodebackward_3_out), .Q(rs_ff_as_3_q));  // open: nQ
  PullUp pullup_5 (.out(pullup_5_out));
  DiodeBackward diodebackward_16 (.in(nRESET), .out(pullup_5_out));
  DiodeBackward diodebackward_17 (.in(nCLK), .out(pullup_5_out));
  D_FF_AS d_ff_as_2 (.Set(1'b0), .D(1'b1), .C(d_ff_as_1_q), .Clr(~pullup_5_out), .Q(d_ff_as_2_q));  // open: nQ
  and and_1 (and_1_out, rs_ff_as_1_q, nSTEPDONE);
  nor nor_1 (nor_1_out, rs_ff_as_2_nq, OP_LATCH);
  DiodeForward diodeforward_1 (.in(d_ff_as_2_q), .out(diodeforward_1_out));
  DiodeForward diodeforward_2 (.in(CLK), .out(diodeforward_1_out));
  DiodeForward diodeforward_3 (.in(and_1_out), .out(diodeforward_1_out));
  DiodeForward diodeforward_4 (.in(nor_1_out), .out(diodeforward_1_out));
  DiodeForward diodeforward_5 (.in(rs_ff_as_3_q), .out(diodeforward_1_out));
  PullDown pulldown_1 (.out(diodeforward_1_out));
  D_FF_AS d_ff_as_3 (.Set(1'b0), .D(1'b1), .C(SLEEP), .Clr(~and_2_out), .nQ(d_ff_as_3_nq));  // open: Q
  and and_2 (and_2_out, nWAKEUP, nRESET);
  D_FF_AS d_ff_as_4 (.Set(1'b0), .D(1'b1), .C(not_2_out), .Clr(~nWAIT_DONE), .nQ(d_ff_as_4_nq));  // open: Q
  not not_2 (not_2_out, nWAIT);
  and and_3 (Running, diodeforward_1_out, d_ff_as_3_nq, d_ff_as_4_nq);
  D_FF d_ff_1 (.D(Running), .C(nRAWCLK), .Q(CLK_EN));  // open: nQ

  // Other names for the same wires on the sheet: RAWCLK = CLK_RAW

  // Notes on the sheet:
  //   Stop: default 1
  //   Run: default 1
  //   One_Instruction: default 1
  //   One_Step: default 1
  //   One_Substep: default 1
  //   nSTEPDONE: default 1
  //   OP_LATCH: default 1
  //   nWAKEUP: default 1
  //   nWAIT_DONE: default 1
endmodule
