// Digital circuit Clock.dig as structural Verilog
module Clock (
  input  CLK,
  input  nCLK,
  input  LEN8,
  input  LEN32,
  input  nLASTSTEP,
  input  nRESET,
  output [4:0] STEP,
  output nLASTSUBSTEP,
  output nSTEPDONE,
  output [7:0] SUBSTEP,
  output nOPDONE
);

  wire not_1_out, or_1_out, switchdt_1_p3, undriven;

  not not_1 (not_1_out, CLK);
  // SwitchDT switchdt_1: pin names not known; wires that end beside it: nCLK, not_1_out, switchdt_1_p3
  Step_Counter step_counter_1 (.CLK(switchdt_1_p3), .nRESET(nRESET), .EN(undriven), .nOPDONE(nOPDONE), .COUNT(STEP));
  Substep_Counter substep_counter_1 (
    .nCLK(switchdt_1_p3), .CLK(nRESET), .nLEN4(LEN8), .EN(LEN32), .nRESET(CLK));  // open: LAST_SUBSTEP, nSTEP_DONE, DVAL, STEP_DONE
  or or_1 (or_1_out, nLASTSUBSTEP, nLASTSTEP);
  D_FF d_ff_1 (.D(or_1_out), .C(CLK), .Q(nOPDONE));  // open: nQ

  // Notes on the sheet:
  //   nLASTSTEP: default 1
endmodule

/* Test case:
CLK ~CLK ~OPDONE ~RESET LEN8 LEN32  STEP ~LASTSUB ~SUBDONE

0   1    1       0      0    0      0    0        X

1   0    1       1      0    0      0    0        X
0   1    1       1      0    0      1    0        X

1   0    1       1      0    0      1    0        X
0   1    1       1      0    0      2    0        X

1   0    1       1      0    0      2    0        X
0   1    1       1      1    0      3    1        0

loop (i,6)
1   0    1       1      1    0      3    1        1
0   1    1       1      1    0      3    1        1
end loop

1   0    1       1      1    0      3    1        1
0   1    1       1      1    0      3    0        1

1   0    1       1      1    0      3    0        0
0   1    1       1      0    0      4    0        0

1   0    1       1      0    0      4    0        0
0   1    1       1      0    1      5    1        0

loop (i,30)
1   0    1       1      0    1      5    1        1
0   1    1       1      0    1      5    1        1
end loop

1   0    1       1      0    1      5    1        1
0   1    1       1      0    1      5    0        1

1   0    1       1      0    1      5    0        0
0   1    1       1      0    1      6    1        0

loop (i,30)
1   0    1       1      0    1      6    1        1
0   1    1       1      0    1      6    1        1
end loop

1   0    1       1      0    1      6    1        1
0   1    1       1      0    1      6    0        1

1   0    1       1      0    1      6    0        0
0   1    1       1      1    0      7    1        0
  
loop (i,6)
1   0    1       1      1    0      7    1        1
0   1    1       1      1    0      7    1        1
end loop

1   0    1       1      1    0      7    1        1
0   1    1       1      1    0      7    0        1

1   0    1       1      1    0      7    0        0
0   1    1       1      0    0      8    0        0

1   0    1       1      0    0      8    0        0
0   1    0       1      1    0      9    1        0

loop (i,6)
1   0    0       1      1    0      9    1        1
0   1    0       1      1    0      9    1        1
end loop

1   0    0       1      1    0      9    1        1
0   1    0       1      1    0      9    0        1

1   0    0       1      1    0      9    0        0
0   1    1       1      0    0      0    0        0
*/
