// Digital circuit Interrupt-Controller.dig as structural Verilog
module Interrupt_Controller (
  input  BUS_CLK,
  input  OP_FETCH,
  input  nTRAP,
  input  nRESET,
  output TRAP_OP,
  output TRAP_OP_FETCH
);

  D_FF_AS #(.Default(1)) d_ff_as_1 (
    .Set(~1'b1), .D(nTRAP), .C(OP_FETCH), .Clr(~nRESET), .nQ(TRAP_OP_FETCH));  // open: Q
  Imm32 u_trap_op (.CLK(BUS_CLK), .nRESET(nRESET), .LATCH(BUS_CLK), .SnP(OP_FETCH), .Val(32'h300073), .OUT(TRAP_OP));
endmodule
