// Digital circuit Mem.dig as structural Verilog
module Mem (
  input  CLK,
  input  BUS_CLK,
  input  IN,
  input  IN_ADDR,
  input  LATCH_ADDR,
  input  CLK_ADDR,
  input  nPE_ADDR,
  input  nOE,
  input  nWE,
  input  nRESET,
  input  [7:0] ROM_DATA,
  input  nS_EXT,
  output OUT,
  output [31:0] ADDR,
  output [7:0] Dout,
  output [7:0] DVal,
  output [7:0] ROM_ADDR,
  output ROM_SEL
);

  wire d_ff_1_nq, d_ff_2_nq, DS, not_1_out;
  wire [7:0] _74hc595_1_qh;

  not not_1 (not_1_out, nWE);
  Mem_addr mem_addr_1 (
    .CLK(BUS_CLK), .IN(IN_ADDR), .LATCH(LATCH_ADDR), .CLK_MEM(CLK_ADDR), .nPE(nPE_ADDR), .nRESET(nRESET),
    .ADDR(ADDR));
  _74HC595 _74hc595_1 (
    .SER(IN), .SRCLK(BUS_CLK), .nSRCLR(nRESET), .RCLK(not_1_out), .nOE(nWE), .VCC(1'b1), .GND(1'b0),
    .QH(_74hc595_1_qh[0]), .QG(_74hc595_1_qh[1]), .QF(_74hc595_1_qh[2]), .QE(_74hc595_1_qh[3]),
    .QD(_74hc595_1_qh[4]), .QC(_74hc595_1_qh[5]), .QB(_74hc595_1_qh[6]), .QA(_74hc595_1_qh[7]));  // open: QH_2
  D_FF #(.Default(1)) d_ff_1 (.D(nOE), .C(CLK), .nQ(d_ff_1_nq));  // open: Q
  Mem_decode mem_decode_1 (
    .ADDR(ADDR), .IN(_74hc595_1_qh), .nOE(nOE), .nWE(nWE), .ROM_DATA(ROM_DATA), .OUT(Dout),
    .ROM_ADDR(ROM_ADDR), .ROM_SEL(ROM_SEL));
  D_FF #(.Default(1)) d_ff_2 (.D(Dout[0]), .C(BUS_CLK), .nQ(d_ff_2_nq));  // open: Q
  PullDown #(.Bits(8)) pulldown_1 (.out(Dout));
  nor nor_1 (DS, nS_EXT, d_ff_2_nq);
  _74HC597 _74hc597_1 (
    .nMR(nRESET), .SHCP(BUS_CLK), .DS(DS), .STCP(d_ff_1_nq), .nPL(nOE), .D7(Dout[0]), .D6(Dout[1]),
    .D5(Dout[2]), .D4(Dout[3]), .D3(Dout[4]), .D2(Dout[5]), .D1(Dout[6]), .D0(Dout[7]), .Q7(OUT), .Val(DVal));

  // Notes on the sheet:
  //   nOE: default 1
  //   nWE: default 1
endmodule

/* Test case:
CLK BUS-CLK IN         ~OE ~WE IN_ADDR      LATCH_ADDR CLK_ADDR ~PE_ADDR ~RESET   OUT

0   0       0          1   1   0            0          0        1        0        0

loop (rep,32)

let addr = 0x00000000 | random(256);

# Output address
loop (i,32)
0   0       0          1   1   (addr>>i&1)  0          0        0        1        X
1   1       0          1   1   (addr>>i&1)  0          0        0        1        X
end loop

# Latch address
0   0       0          1   1   0            1          0        0        1        X
1   0       0          1   1   0            1          1        0        1        X

# Enable output and latch
0   0       0          0   1   0            0          0        1        1        X
1   0       0          0   1   0            0          0        1        1        X

# Output data
loop (i,8)
0   0       0          1   1   0            0          0        1        1        (addr>>i&1)
1   1       0          1   1   0            0          0        1        1        X
end loop

let addr = 0x80000000 | random(256);
let d0 = random(256);
let d1 = random(256);
let d2 = random(256);
let d3 = random(256);

# Output address
loop (i,32)
0   0       0          1   1   (addr>>i&1)  0          0        0        1        X
1   1       0          1   1   (addr>>i&1)  0          0        0        1        X
end loop

# Latch address
0   0       0          1   1   0            1          0        0        1        X
1   0       0          1   1   0            1          1        0        1        X

# Output data
loop (i,8)
0   0       (d0>>i&1)  1   1   0            0          0        1        1        X
1   1       (d0>>i&1)  1   1   0            0          0        1        1        X
end loop

# Latch data and write
0   0       0          1   1   0            0          0        1        1        X
0   0       0          1   0   0            0          0        1        1        X

# Output data and increase address
loop (i,8)
0   0       (d1>>i&1)  1   1   0            0          1        1        1        X
1   1       (d1>>i&1)  1   1   0            0          1        1        1        X
end loop

# Latch data and write
0   0       0          1   1   0            0          0        1        1        X
0   0       0          1   0   0            0          0        1        1        X

# Output data and increase address
loop (i,8)
0   0       (d2>>i&1)  1   1   0            0          1        1        1        X
1   1       (d2>>i&1)  1   1   0            0          1        1        1        X
end loop

# Latch data and write
0   0       0          1   1   0            0          0        1        1        X
0   0       0          1   0   0            0          0        1        1        X

# Output data and increase address
loop (i,8)
0   0       (d3>>i&1)  1   1   0            0          1        1        1        X
1   1       (d3>>i&1)  1   1   0            0          1        1        1        X
end loop

# Latch data and write
0   0       0          1   1   0            0          0        1        1        X
0   0       0          1   0   0            0          0        1        1        X

# Output address
loop (i,32)
0   0       0          1   1   (addr>>i&1)  0          0        0        1        X
1   1       0          1   1   (addr>>i&1)  0          0        0        1        X
end loop

# Latch address
0   0       0          1   1   0            1          0        0        1        X
1   0       0          1   1   0            1          1        0        1        X

# Enable output and latch
0   0       0          0   1   0            0          0        1        1        X
1   0       0          0   1   0            0          0        1        1        X

# Output data and increase address
loop (i,8)
0   0       0          1   1   0            0          1        1        1        (d0>>i&1)
1   1       0          1   1   0            0          1        1        1        X
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*/
